# Fritzing sketch Exercise 1 (saved by Fritzing 0.9.10b)
breadboards: 1

parts:
  Part1 = Arduino Uno (Rev3)
  LED1 = LED - 5mm [color="Red (633nm)" current=0.030 package="5 mm [THT]"]
  R1 = Resistor [tolerance=±5% power=0.25 resistance=220 package=THT]

nets:
  N1: Part1.GND, LED1.anode
  N2: Part1.D5_PWM, R1.Pin_0
  N3: LED1.cathode, R1.Pin_1
