# Fritzing sketch Exercise 4 (saved by Fritzing 0.9.10b)
breadboards: 1

parts:
  Part1 = Arduino Uno (Rev3)
  LED3 = smd LED [color="Red (633nm)" package="1206 [SMD]"]
  R3 = Resistor [tolerance=±5% resistance=220 package="1206 [SMD]"]
  S1 = Pushbutton [package="[SMD]"]

nets:
  N1: Part1.GND, R3.Pin_0, S1.Pin_3, S1.Pin_4
  N2: Part1.D2, S1.Pin_1, S1.Pin_2
  N3: Part1.D5_PWM, LED3.cathode
  N4: LED3.anode, R3.Pin_1
